# Fritzing sketch Schematics 4 Weather station (saved by Fritzing 0.8.7b)
breadboards: 1

parts:
  U1 = ESP32S-HiLetgo [part_number=ESP32S-HiLetgo]
  M1 = BMP280
  U2 = LM2596 step down module
  LED2 = LED - 5mm [color="Green (555nm)" package="5 mm [THT]"]
  LED1 = LED - 5mm [color="Red (633nm)" package="5 mm [THT]"]
  R3 = Resistor [package="2010 [SMD]"]
  R4 = Resistor [package="2010 [SMD]"]
  YL-83_-_Control_Board1 = YL-83 Rain Sensor - Control Board
  YL-83_-_Detection_Board1 = YL-83 Rain Sensor - Detection Board

nets:
  VIN: U1.3.3, M1.VIN, U2.IN+, YL-83_-_Control_Board1.VCC
  N1: U1.GPIO25, R4.Pin_0
  N2: U1.GPIO27, YL-83_-_Control_Board1.DO
  N3: U1.GPIO19, R3.Pin_0
  N4: U1.GPIO21, M1.SDA
  N5: U1.GPIO22, M1.SCL
  GND: U1.GND, M1.GND, U2.IN-, U2.OUT-, LED2.cathode, LED1.cathode, YL-83_-_Control_Board1.GND
  N6: LED2.anode, R4.Pin_1
  N7: LED1.anode, R3.Pin_1
  N8: YL-83_-_Control_Board1.POS, YL-83_-_Detection_Board1.POS
  N9: YL-83_-_Control_Board1.NEG, YL-83_-_Detection_Board1.NEG

notes:
  * Voltage Output
  * Power +
  * Ground -
  Anemometer

custom parts:
  ESP32S-HiLetgo: HiLetgo ESP-WROOM-32 ESP32 ESP-32S Development Board 2.4GHz Dual-Mode WiFi + Bluetooth Dual Cores Microcontroller The ESP32 integrated with Antenna switches, RF Balun, power amplifiers, low-noise amplifiers, filters, and management modules, and the entire solution occupies the least area of PCB. 2.4 GHz Wi-Fi plus Bluetooth dual-mode chip, with TSMC Ultra-low power consumption 40nm technology,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
  BMP280: Temperature Humidity Barometric presure Sensor, I2C
  LM2596 step down module: LM2596 DC-DC step down power supply module 3 A.
  YL-83 Rain Sensor - Control Board: The YL-83 is a rain sensor that has more resistance when dry and less resistance when wet. The module runs at 5V.
  YL-83 Rain Sensor - Detection Board: The YL-83 is a rain sensor that has more resistance when dry and less resistance when wet. The module runs at 5V.
